# Fritzing sketch Projeto-01-Arduino (saved by Fritzing 0.9.3b)
breadboards: 1

parts:
  R1 = Photocell (LDR) [package=THT]
  R2 = Resistor [tolerance=±5% resistance=220 package="0805 [SMD]"]
  U1 = ESP8266 NodeMCU LoLin module
  LED1 = LEDs [package=led10mm]
  R3 = Resistor [tolerance=±5% resistance=220 package="0805 [SMD]"]

nets:
  N1: R1.pin_1, R2.Pin_0, U1.D2
  N2: U1.D1, LED1.A
  N3: U1.3V3, R3.Pin_0
  N4: LED1.C, R3.Pin_1

custom parts:
  ESP8266 NodeMCU LoLin module: ESP8266 based NodeMCU
